// Logisim project LabA.circ as structural Verilog: 1 circuit, main circuit main
module main (
  input  in_1,
  input  in_2,
  input  in_3,
  input  in_4,
  input  A,
  input  in_6,
  input  in_7,
  input  B,
  input  C,
  input  in_10,
  input  D,
  input  in_12,
  input  in_13,
  input  in_14,
  output out_15,
  output out_16,
  output out_17,
  output F,
  output out_19,
  output out_20
);

  wire and_2_out, and_3_out, nand_1_out, nand_2_out, nand_3_out, nand_4_out, nand_7_out, nand_8_out,
       nand_9_out, nand_10_out, nand_11_out, nand_12_out, nand_13_out, nand_14_out, not_1_out, not_2_out;

  not not_1 (not_1_out, in_1);
  not not_2 (not_2_out, in_2);
  and and_1 (out_16, in_3, in_4);
  nor nor_1 (out_17, in_6, in_7);
  nand nand_1 (nand_1_out, in_10, in_12);
  nand nand_2 (nand_2_out, in_10, in_12);
  nand nand_3 (nand_3_out, in_13, nand_4_out);
  nand nand_4 (nand_4_out, nand_3_out, in_14);
  and and_2 (and_2_out, not_1_out, in_2);
  and and_3 (and_3_out, in_1, not_2_out);
  nand nand_5 (out_19, nand_1_out, nand_2_out);
  nand nand_6 (out_20, nand_3_out, nand_4_out);
  or or_1 (out_15, and_2_out, and_3_out);
  nand nand_7 (nand_7_out, A, B);
  nand nand_8 (nand_8_out, A, B);
  nand nand_9 (nand_9_out, C, D);
  nand nand_10 (nand_10_out, C, D);
  nand nand_11 (nand_11_out, nand_7_out, nand_8_out);
  nand nand_12 (nand_12_out, nand_9_out, nand_10_out);
  nand nand_13 (nand_13_out, nand_11_out, nand_14_out);
  nand nand_14 (nand_14_out, nand_13_out, nand_12_out);
  nand nand_15 (F, nand_13_out, nand_14_out);

  // Notes on the sheet:
  //   AND Gate
  //   NOR Gate
  //   AND Gate Design
  //   OR Gate Design
  //   XOR Circuit
  //   F= AB + CD
  //   September 13, 2019
  //   Ryan Sullivan
endmodule
